// Logisim project BranchingComputer.circ as structural Verilog: 25 circuits, main circuit main
module main (
);

  wire alu3_1_zflag, and_1_out, blu_1_bluout, C, control2_1_alusrc, control2_1_cbr, control2_1_linkreg,
       control2_1_memtoreg, control2_1_memwrite, control2_1_pbr, control2_1_reg2loc, control2_1_regwrite,
       control2_1_ubr, decoder7seg_1_a, decoder7seg_1_b, decoder7seg_1_c, decoder7seg_1_d, decoder7seg_1_dp,
       decoder7seg_1_e, decoder7seg_1_f, decoder7seg_1_g, decoder7seg_2_a, decoder7seg_2_b, decoder7seg_2_c,
       decoder7seg_2_d, decoder7seg_2_dp, decoder7seg_2_e, decoder7seg_2_f, decoder7seg_2_g, decoder7seg_3_a,
       decoder7seg_3_b, decoder7seg_3_c, decoder7seg_3_d, decoder7seg_3_dp, decoder7seg_3_e, decoder7seg_3_f,
       decoder7seg_3_g, decoder7seg_4_a, decoder7seg_4_b, decoder7seg_4_c, decoder7seg_4_d, decoder7seg_4_dp,
       decoder7seg_4_e, decoder7seg_4_f, decoder7seg_4_g, decoder7seg_5_a, decoder7seg_5_b, decoder7seg_5_c,
       decoder7seg_5_d, decoder7seg_5_dp, decoder7seg_5_e, decoder7seg_5_f, decoder7seg_5_g, decoder7seg_6_a,
       decoder7seg_6_b, decoder7seg_6_c, decoder7seg_6_d, decoder7seg_6_dp, decoder7seg_6_e, decoder7seg_6_f,
       decoder7seg_6_g, decoder7seg_7_a, decoder7seg_7_b, decoder7seg_7_c, decoder7seg_7_d, decoder7seg_7_dp,
       decoder7seg_7_e, decoder7seg_7_f, decoder7seg_7_g, decoder7seg_8_a, decoder7seg_8_b, decoder7seg_8_c,
       decoder7seg_8_d, decoder7seg_8_dp, decoder7seg_8_e, decoder7seg_8_f, decoder7seg_8_g, or_1_out;
  wire [1:0] control2_1_bytestouse;
  wire [3:0] action, alu3_1_ccodes, control2_1_bluop;
  wire [4:0] instdec_1_rd, instdec_1_rm, instdec_1_rn, instdec_1_rt, multiplexer_1_out;
  wire [7:0] charto7seg_1_num, charto7seg_2_num, charto7seg_3_num, charto7seg_4_num, charto7seg_5_num,
       charto7seg_6_num, charto7seg_7_num, charto7seg_8_num;
  wire [10:0] instdec_1_imm, instdec_1_immcopy, instdec_1_opcodecopy;
  wire [15:0] addbrpc_1_brpc, brmux_1_pcin, pc_1_pcout, pcadder_1_nextrpc;
  wire [31:0] instructionmemory_1_instruction;
  wire [63:0] alu3_1_aluout, alumux_1_alumuxout, datamemory_1_readdatam, regfile_1_regdata1,
       regfile_1_regdata2, regfile_1_regdata3, writebackmux_1_regdataw, zeroregister;

  PCAdder pcadder_1 (.PC(pc_1_pcout), .NextrPC(pcadder_1_nextrpc));
  ADDBrPC addbrpc_1 (.Imm(instdec_1_immcopy), .PC(pc_1_pcout), .BrPC(addbrpc_1_brpc));
  and and_1 (and_1_out, control2_1_cbr, blu_1_bluout);
  or or_1 (or_1_out, and_1_out, control2_1_ubr);
  BrMUX brmux_1 (
    .ALUout(alu3_1_aluout), .PBr(control2_1_pbr), .Br(or_1_out), .NextPC(pcadder_1_nextrpc),
    .BrPC(addbrpc_1_brpc), .PCin(brmux_1_pcin));
  BLU blu_1 (.action(control2_1_bluop), .Ccodes(alu3_1_ccodes), .ZnotCode(alu3_1_zflag), .BLUout(blu_1_bluout));
  Control2 control2_1 (
    .Opcode(instdec_1_opcodecopy), .BLUop(control2_1_bluop), .ALUop(action),
    .bytesToUse(control2_1_bytestouse), .RegWrite(control2_1_regwrite), .LinkReg(control2_1_linkreg),
    .Pbr(control2_1_pbr), .Ubr(control2_1_ubr), .Cbr(control2_1_cbr), .MemToReg(control2_1_memtoreg),
    .MemWrite(control2_1_memwrite), .ALUsrc(control2_1_alusrc), .Reg2Loc(control2_1_reg2loc));
  InstDec instdec_1 (
    .Instruction(instructionmemory_1_instruction), .OpcodeCopy(instdec_1_opcodecopy), .Rm(instdec_1_rm),
    .Rn(instdec_1_rn), .Rt(instdec_1_rt), .immCopy(instdec_1_immcopy), .imm(instdec_1_imm), .Rd(instdec_1_rd));  // open: Opcode
  Multiplexer #(.width(5)) multiplexer_1 (
    .in0(instdec_1_rt), .in1(instdec_1_rm), .out(multiplexer_1_out), .sel(control2_1_reg2loc));
  DataMemory datamemory_1 (
    .bytesToUse(control2_1_bytestouse), .Address(alu3_1_aluout), .WriteDataM(regfile_1_regdata3), .Clock(C),
    .MemWrite(control2_1_memwrite), .ReadDataM(datamemory_1_readdatam));
  ALUMUX alumux_1 (
    .Imm(instdec_1_imm), .RegData2(regfile_1_regdata2), .ALUsrc(control2_1_alusrc),
    .ALUMUXout(alumux_1_alumuxout));
  ALU3 alu3_1 (
    .clock(C), .action(action), .A(regfile_1_regdata1), .B(alumux_1_alumuxout), .ALUout(alu3_1_aluout),
    .Zflag(alu3_1_zflag), .cCodes(alu3_1_ccodes));
  PC pc_1 (.NextPC(brmux_1_pcin), .Clock(C), .PCout(pc_1_pcout));
  InstructionMemory instructionmemory_1 (.Clock(C), .PC(pc_1_pcout), .Instruction(instructionmemory_1_instruction));
  RegFile regfile_1 (
    .Clock(C), .RegWrite(control2_1_regwrite), .WriteReg(instdec_1_rd), .ReadReg1(instdec_1_rn),
    .ReadReg2(multiplexer_1_out), .ReadReg3(instdec_1_rt), .RegDataW(writebackmux_1_regdataw),
    .reg0(zeroregister), .RegData1(regfile_1_regdata1), .RegData2(regfile_1_regdata2),
    .RegData3(regfile_1_regdata3));
  WriteBackMUX writebackmux_1 (
    .MemToReg(control2_1_memtoreg), .LinkReg(control2_1_linkreg), .ALUout(alu3_1_aluout),
    .ReadDataM(datamemory_1_readdatam), .NextPC(pcadder_1_nextrpc), .RegDataW(writebackmux_1_regdataw));
  Clock clock_1 (.out(C));
  Hex_Digit_Display hex_digit_display_1 (.value(zeroregister[63:60]));  // open: dp
  _7_Segment_Display u_7_segment_display_1 (
    .g(decoder7seg_1_g), .f(decoder7seg_1_f), .a(decoder7seg_1_a), .b(decoder7seg_1_b), .e(decoder7seg_1_e),
    .d(decoder7seg_1_d), .c(decoder7seg_1_c), .dp(decoder7seg_1_dp));
  Hex_Digit_Display hex_digit_display_2 (.value(zeroregister[59:56]));  // open: dp
  Hex_Digit_Display hex_digit_display_3 (.value(zeroregister[55:52]));  // open: dp
  decoder7Seg decoder7seg_1 (
    .num(charto7seg_1_num), .F(decoder7seg_1_f), .G(decoder7seg_1_g), .E(decoder7seg_1_e),
    .D(decoder7seg_1_d), .A(decoder7seg_1_a), .B(decoder7seg_1_b), .DP(decoder7seg_1_dp), .C(decoder7seg_1_c));
  decoder7Seg decoder7seg_2 (
    .num(charto7seg_2_num), .F(decoder7seg_2_f), .G(decoder7seg_2_g), .E(decoder7seg_2_e),
    .D(decoder7seg_2_d), .A(decoder7seg_2_a), .B(decoder7seg_2_b), .DP(decoder7seg_2_dp), .C(decoder7seg_2_c));
  _7_Segment_Display u_7_segment_display_2 (
    .g(decoder7seg_2_g), .f(decoder7seg_2_f), .a(decoder7seg_2_a), .b(decoder7seg_2_b), .e(decoder7seg_2_e),
    .d(decoder7seg_2_d), .c(decoder7seg_2_c), .dp(decoder7seg_2_dp));
  _7_Segment_Display u_7_segment_display_3 (
    .g(decoder7seg_3_g), .f(decoder7seg_3_f), .a(decoder7seg_3_a), .b(decoder7seg_3_b), .e(decoder7seg_3_e),
    .d(decoder7seg_3_d), .c(decoder7seg_3_c), .dp(decoder7seg_3_dp));
  charTo7Seg charto7seg_1 (.char(zeroregister[63:56]), .num(charto7seg_1_num));
  charTo7Seg charto7seg_2 (.char(zeroregister[55:48]), .num(charto7seg_2_num));
  Hex_Digit_Display hex_digit_display_4 (.value(zeroregister[51:48]));  // open: dp
  Hex_Digit_Display hex_digit_display_5 (.value(zeroregister[47:44]));  // open: dp
  decoder7Seg decoder7seg_3 (
    .num(charto7seg_3_num), .F(decoder7seg_3_f), .G(decoder7seg_3_g), .E(decoder7seg_3_e),
    .D(decoder7seg_3_d), .A(decoder7seg_3_a), .B(decoder7seg_3_b), .DP(decoder7seg_3_dp), .C(decoder7seg_3_c));
  _7_Segment_Display u_7_segment_display_4 (
    .g(decoder7seg_4_g), .f(decoder7seg_4_f), .a(decoder7seg_4_a), .b(decoder7seg_4_b), .e(decoder7seg_4_e),
    .d(decoder7seg_4_d), .c(decoder7seg_4_c), .dp(decoder7seg_4_dp));
  charTo7Seg charto7seg_3 (.char(zeroregister[47:40]), .num(charto7seg_3_num));
  Hex_Digit_Display hex_digit_display_6 (.value(zeroregister[43:40]));  // open: dp
  Hex_Digit_Display hex_digit_display_7 (.value(zeroregister[39:36]));  // open: dp
  decoder7Seg decoder7seg_4 (
    .num(charto7seg_4_num), .F(decoder7seg_4_f), .G(decoder7seg_4_g), .E(decoder7seg_4_e),
    .D(decoder7seg_4_d), .A(decoder7seg_4_a), .B(decoder7seg_4_b), .DP(decoder7seg_4_dp), .C(decoder7seg_4_c));
  decoder7Seg decoder7seg_5 (
    .num(charto7seg_5_num), .F(decoder7seg_5_f), .G(decoder7seg_5_g), .E(decoder7seg_5_e),
    .D(decoder7seg_5_d), .A(decoder7seg_5_a), .B(decoder7seg_5_b), .DP(decoder7seg_5_dp), .C(decoder7seg_5_c));
  _7_Segment_Display u_7_segment_display_5 (
    .g(decoder7seg_5_g), .f(decoder7seg_5_f), .a(decoder7seg_5_a), .b(decoder7seg_5_b), .e(decoder7seg_5_e),
    .d(decoder7seg_5_d), .c(decoder7seg_5_c), .dp(decoder7seg_5_dp));
  _7_Segment_Display u_7_segment_display_6 (
    .g(decoder7seg_6_g), .f(decoder7seg_6_f), .a(decoder7seg_6_a), .b(decoder7seg_6_b), .e(decoder7seg_6_e),
    .d(decoder7seg_6_d), .c(decoder7seg_6_c), .dp(decoder7seg_6_dp));
  charTo7Seg charto7seg_4 (.char(zeroregister[39:32]), .num(charto7seg_4_num));
  charTo7Seg charto7seg_5 (.char(zeroregister[31:24]), .num(charto7seg_5_num));
  Hex_Digit_Display hex_digit_display_8 (.value(zeroregister[35:32]));  // open: dp
  Hex_Digit_Display hex_digit_display_9 (.value(zeroregister[31:28]));  // open: dp
  decoder7Seg decoder7seg_6 (
    .num(charto7seg_6_num), .F(decoder7seg_6_f), .G(decoder7seg_6_g), .E(decoder7seg_6_e),
    .D(decoder7seg_6_d), .A(decoder7seg_6_a), .B(decoder7seg_6_b), .DP(decoder7seg_6_dp), .C(decoder7seg_6_c));
  decoder7Seg decoder7seg_7 (
    .num(charto7seg_7_num), .F(decoder7seg_7_f), .G(decoder7seg_7_g), .E(decoder7seg_7_e),
    .D(decoder7seg_7_d), .A(decoder7seg_7_a), .B(decoder7seg_7_b), .DP(decoder7seg_7_dp), .C(decoder7seg_7_c));
  _7_Segment_Display u_7_segment_display_7 (
    .g(decoder7seg_7_g), .f(decoder7seg_7_f), .a(decoder7seg_7_a), .b(decoder7seg_7_b), .e(decoder7seg_7_e),
    .d(decoder7seg_7_d), .c(decoder7seg_7_c), .dp(decoder7seg_7_dp));
  charTo7Seg charto7seg_6 (.char(zeroregister[23:16]), .num(charto7seg_6_num));
  charTo7Seg charto7seg_7 (.char(zeroregister[15:8]), .num(charto7seg_7_num));
  Hex_Digit_Display hex_digit_display_10 (.value(zeroregister[27:24]));  // open: dp
  Hex_Digit_Display hex_digit_display_11 (.value(zeroregister[23:20]));  // open: dp
  decoder7Seg decoder7seg_8 (
    .num(charto7seg_8_num), .F(decoder7seg_8_f), .G(decoder7seg_8_g), .E(decoder7seg_8_e),
    .D(decoder7seg_8_d), .A(decoder7seg_8_a), .B(decoder7seg_8_b), .DP(decoder7seg_8_dp), .C(decoder7seg_8_c));
  _7_Segment_Display u_7_segment_display_8 (
    .g(decoder7seg_8_g), .f(decoder7seg_8_f), .a(decoder7seg_8_a), .b(decoder7seg_8_b), .e(decoder7seg_8_e),
    .d(decoder7seg_8_d), .c(decoder7seg_8_c), .dp(decoder7seg_8_dp));
  charTo7Seg charto7seg_8 (.char(zeroregister[7:0]), .num(charto7seg_8_num));
  Hex_Digit_Display hex_digit_display_12 (.value(zeroregister[19:16]));  // open: dp
  Hex_Digit_Display hex_digit_display_13 (.value(zeroregister[15:12]));  // open: dp
  Hex_Digit_Display hex_digit_display_14 (.value(zeroregister[11:8]));  // open: dp
  Hex_Digit_Display hex_digit_display_15 (.value(zeroregister[7:4]));  // open: dp
  Hex_Digit_Display hex_digit_display_16 (.value(zeroregister[3:0]));  // open: dp

  // Notes on the sheet:
  //   PCin
  //   NextPC
  //   NextPC
  //   PC
  //   imm + PC
  //   Cbr
  //   Pbr
  //   Br
  //   PCin
  //   Ubr
  //   ALUout
  //   BLUop
  //   codes
  //   CPUname: branchingCPU Kian Holden. I pledge my honor that I have abided by the Stevens Honor System.
  //   RegWrite
  //   ALUsrc
  //   bytesToUse
  //   Reg2Loc
  //   R[n]
  //   Z
  //   MemWrite
  //   LinkReg
  //   R[t|m]
  //   ALUout
  //   MemToReg
  //   NextPC
  //   t
  //   R[t]
  //   d
  //   imm
  //   ALUout
  //   RegDataW
  //   Clock
  //   RegDataW
endmodule

module PC (
  input  [15:0] NextPC,
  input  Clock,
  output [15:0] PCout
);

  Register #(.width(16)) register_1 (.D(NextPC), .en(1'b1), .clk(Clock), .Q(PCout));  // open: clr
endmodule

module PCAdder (
  input  [15:0] PC,
  output [15:0] NextrPC
);

  Adder #(.width(16)) adder_1 (.a(PC), .b(16'h1), .out(NextrPC));  // open: cin, cout
endmodule

module InstructionMemory (
  input  [15:0] PC,
  input  Clock,
  output [31:0] Instruction
);

  wire not_1_out;

  not not_1 (not_1_out, 1'b0);
  RAM #(.addrWidth(16), .dataWidth(32), .enables("line")) ram_1 (
    .addr(PC), .we(1'b0), .oe(not_1_out), .clk(Clock), .dout(Instruction));  // open: din

  // Notes on the sheet:
  //   B 7 = 00100000010 0000000000 00000000111
  //   BL 4 = 6040F004
endmodule

module InstDec (
  input  [31:0] Instruction,
  output [4:0] Rm,
  output [10:0] immCopy,
  output [10:0] imm,
  output [4:0] Rn,
  output [4:0] Rt,
  output [10:0] OpcodeCopy,
  output [4:0] Rd,
  output [10:0] Opcode
);


  assign imm = Instruction[10:0];
  assign immCopy = Instruction[10:0];
  assign Opcode = Instruction[31:21];
  assign OpcodeCopy = Instruction[31:21];
  assign Rd = Instruction[20:16];
  assign Rm = Instruction[4:0];
  assign Rn = Instruction[15:11];
  assign Rt = Instruction[20:16];

  // Notes on the sheet:
  //   ALUop/ 00 is passb. 01 is +, 10 is x, 11 is -
  //   If memwrite or memread, then ALUop bits can determine how many bytes to read/write
  //   B, 7 = 0x20401e00
  //   MOVimm X0, 2 = 08400800 
  //   MOVimm X0, 7 = 08401c00
  //   CBZ X3, 2 = 10000c03
  //   MOV X0, -1 = 085ffc00
  //   CBZ X0, 5 = 10001400
endmodule

module RegFile (
  input  [4:0] WriteReg,
  input  [4:0] ReadReg1,
  input  [4:0] ReadReg2,
  input  [4:0] ReadReg3,
  input  [63:0] RegDataW,
  input  Clock,
  input  RegWrite,
  output [63:0] RegData1,
  output [63:0] RegData2,
  output [63:0] RegData3,
  output [63:0] reg0
);

  wire and_1_out, and_2_out, and_3_out, and_4_out, and_5_out, and_6_out, and_7_out, and_8_out, and_9_out,
       and_10_out, and_11_out, and_12_out, and_13_out, and_14_out, and_15_out, and_16_out, and_17_out,
       and_18_out, and_19_out, and_20_out, and_21_out, and_22_out, and_23_out, and_24_out, and_25_out,
       and_26_out, and_27_out, and_28_out, and_29_out, and_30_out, and_31_out, and_32_out, decoder_1_out0,
       decoder_1_out1, decoder_1_out2, decoder_1_out3, decoder_1_out4, decoder_1_out5, decoder_1_out6,
       decoder_1_out7, decoder_1_out8, decoder_1_out9, decoder_1_out10, decoder_1_out11, decoder_1_out12,
       decoder_1_out13, decoder_1_out14, decoder_1_out15, decoder_1_out16, decoder_1_out17, decoder_1_out18,
       decoder_1_out19, decoder_1_out20, decoder_1_out21, decoder_1_out22, decoder_1_out23, decoder_1_out24,
       decoder_1_out25, decoder_1_out26, decoder_1_out27, decoder_1_out28, decoder_1_out29, decoder_1_out30,
       decoder_1_out31;
  wire [63:0] X1_q, X2_q, X3_q, X4_q, X5_q, X6_q, X7_q, X8_q, X9_q, X10_q, X11_q, X12_q, X13_q, X14_q, X15_q,
       X16_q, X17_q, X18_q, X19_q, X20_q, X21_q, X22_q, X23_q, X24_q, X25_q, X26_q, X27_q, X28_q, X29_q,
       X30_q;

  Decoder #(.enable("false"), .select(5)) decoder_1 (
    .out0(decoder_1_out0), .out1(decoder_1_out1), .out2(decoder_1_out2), .out3(decoder_1_out3),
    .out4(decoder_1_out4), .out5(decoder_1_out5), .out6(decoder_1_out6), .out7(decoder_1_out7),
    .out8(decoder_1_out8), .out9(decoder_1_out9), .out10(decoder_1_out10), .out11(decoder_1_out11),
    .out12(decoder_1_out12), .out13(decoder_1_out13), .out14(decoder_1_out14), .out15(decoder_1_out15),
    .out16(decoder_1_out16), .out17(decoder_1_out17), .out18(decoder_1_out18), .out19(decoder_1_out19),
    .out20(decoder_1_out20), .out21(decoder_1_out21), .out22(decoder_1_out22), .out23(decoder_1_out23),
    .out24(decoder_1_out24), .out25(decoder_1_out25), .out26(decoder_1_out26), .out27(decoder_1_out27),
    .out28(decoder_1_out28), .out29(decoder_1_out29), .out30(decoder_1_out30), .out31(decoder_1_out31),
    .sel(WriteReg));
  Register #(.width(64)) X0 (.D(RegDataW), .en(and_1_out), .clk(Clock), .Q(reg0));  // open: clr
  and and_1 (and_1_out, RegWrite, decoder_1_out0);
  Register #(.width(64)) X1 (.D(RegDataW), .en(and_2_out), .clk(Clock), .Q(X1_q));  // open: clr
  and and_2 (and_2_out, RegWrite, decoder_1_out1);
  Register #(.width(64)) X2 (.D(RegDataW), .en(and_3_out), .clk(Clock), .Q(X2_q));  // open: clr
  and and_3 (and_3_out, RegWrite, decoder_1_out2);
  Register #(.width(64)) X3 (.D(RegDataW), .en(and_4_out), .clk(Clock), .Q(X3_q));  // open: clr
  and and_4 (and_4_out, RegWrite, decoder_1_out3);
  Register #(.width(64)) X4 (.D(RegDataW), .en(and_5_out), .clk(Clock), .Q(X4_q));  // open: clr
  and and_5 (and_5_out, RegWrite, decoder_1_out4);
  Register #(.width(64)) X5 (.D(RegDataW), .en(and_6_out), .clk(Clock), .Q(X5_q));  // open: clr
  and and_6 (and_6_out, RegWrite, decoder_1_out5);
  Register #(.width(64)) X6 (.D(RegDataW), .en(and_7_out), .clk(Clock), .Q(X6_q));  // open: clr
  and and_7 (and_7_out, RegWrite, decoder_1_out6);
  Register #(.width(64)) X7 (.D(RegDataW), .en(and_8_out), .clk(Clock), .Q(X7_q));  // open: clr
  and and_8 (and_8_out, RegWrite, decoder_1_out7);
  Register #(.width(64)) X8 (.D(RegDataW), .en(and_9_out), .clk(Clock), .Q(X8_q));  // open: clr
  and and_9 (and_9_out, RegWrite, decoder_1_out8);
  Register #(.width(64)) X9 (.D(RegDataW), .en(and_10_out), .clk(Clock), .Q(X9_q));  // open: clr
  and and_10 (and_10_out, RegWrite, decoder_1_out9);
  Register #(.width(64)) X10 (.D(RegDataW), .en(and_11_out), .clk(Clock), .Q(X10_q));  // open: clr
  and and_11 (and_11_out, RegWrite, decoder_1_out10);
  Register #(.width(64)) X11 (.D(RegDataW), .en(and_12_out), .clk(Clock), .Q(X11_q));  // open: clr
  and and_12 (and_12_out, RegWrite, decoder_1_out11);
  Register #(.width(64)) X12 (.D(RegDataW), .en(and_13_out), .clk(Clock), .Q(X12_q));  // open: clr
  and and_13 (and_13_out, RegWrite, decoder_1_out12);
  Register #(.width(64)) X13 (.D(RegDataW), .en(and_14_out), .clk(Clock), .Q(X13_q));  // open: clr
  and and_14 (and_14_out, RegWrite, decoder_1_out13);
  Register #(.width(64)) X14 (.D(RegDataW), .en(and_15_out), .clk(Clock), .Q(X14_q));  // open: clr
  and and_15 (and_15_out, RegWrite, decoder_1_out14);
  Register #(.width(64)) X15 (.D(RegDataW), .en(and_16_out), .clk(Clock), .Q(X15_q));  // open: clr
  and and_16 (and_16_out, RegWrite, decoder_1_out15);
  Register #(.width(64)) X16 (.D(RegDataW), .en(and_17_out), .clk(Clock), .Q(X16_q));  // open: clr
  and and_17 (and_17_out, RegWrite, decoder_1_out16);
  Register #(.width(64)) X17 (.D(RegDataW), .en(and_18_out), .clk(Clock), .Q(X17_q));  // open: clr
  and and_18 (and_18_out, RegWrite, decoder_1_out17);
  Register #(.width(64)) X18 (.D(RegDataW), .en(and_19_out), .clk(Clock), .Q(X18_q));  // open: clr
  and and_19 (and_19_out, RegWrite, decoder_1_out18);
  Register #(.width(64)) X19 (.D(RegDataW), .en(and_20_out), .clk(Clock), .Q(X19_q));  // open: clr
  and and_20 (and_20_out, RegWrite, decoder_1_out19);
  Register #(.width(64)) X20 (.D(RegDataW), .en(and_21_out), .clk(Clock), .Q(X20_q));  // open: clr
  and and_21 (and_21_out, RegWrite, decoder_1_out20);
  Register #(.width(64)) X21 (.D(RegDataW), .en(and_22_out), .clk(Clock), .Q(X21_q));  // open: clr
  and and_22 (and_22_out, RegWrite, decoder_1_out21);
  Register #(.width(64)) X22 (.D(RegDataW), .en(and_23_out), .clk(Clock), .Q(X22_q));  // open: clr
  and and_23 (and_23_out, RegWrite, decoder_1_out22);
  Register #(.width(64)) X23 (.D(RegDataW), .en(and_24_out), .clk(Clock), .Q(X23_q));  // open: clr
  and and_24 (and_24_out, RegWrite, decoder_1_out23);
  Register #(.width(64)) X24 (.D(RegDataW), .en(and_25_out), .clk(Clock), .Q(X24_q));  // open: clr
  and and_25 (and_25_out, RegWrite, decoder_1_out24);
  Register #(.width(64)) X25 (.D(RegDataW), .en(and_26_out), .clk(Clock), .Q(X25_q));  // open: clr
  and and_26 (and_26_out, RegWrite, decoder_1_out25);
  Register #(.width(64)) X26 (.D(RegDataW), .en(and_27_out), .clk(Clock), .Q(X26_q));  // open: clr
  and and_27 (and_27_out, RegWrite, decoder_1_out26);
  Register #(.width(64)) X27 (.D(RegDataW), .en(and_28_out), .clk(Clock), .Q(X27_q));  // open: clr
  and and_28 (and_28_out, RegWrite, decoder_1_out27);
  Register #(.width(64)) X28 (.D(RegDataW), .en(and_29_out), .clk(Clock), .Q(X28_q));  // open: clr
  and and_29 (and_29_out, RegWrite, decoder_1_out28);
  Register #(.width(64)) X29 (.D(RegDataW), .en(and_30_out), .clk(Clock), .Q(X29_q));  // open: clr
  and and_30 (and_30_out, RegWrite, decoder_1_out29);
  Register #(.width(64)) X30 (.D(RegDataW), .en(and_31_out), .clk(Clock), .Q(X30_q));  // open: clr
  and and_31 (and_31_out, RegWrite, decoder_1_out30);
  Register #(.width(64)) X31 (.D(RegDataW), .en(and_32_out), .clk(Clock));  // open: Q, clr
  and and_32 (and_32_out, RegWrite, decoder_1_out31);
  Multiplexer #(.select(5), .width(64)) multiplexer_1 (
    .in0(reg0), .in1(X1_q), .in2(X2_q), .in3(X3_q), .in4(X4_q), .in5(X5_q), .in6(X6_q), .in7(X7_q),
    .in8(X8_q), .in9(X9_q), .in10(X10_q), .in11(X11_q), .in12(X12_q), .in13(X13_q), .in14(X14_q),
    .in15(X15_q), .in16(X16_q), .in17(X17_q), .in18(X18_q), .in19(X19_q), .in20(X20_q), .in21(X21_q),
    .in22(X22_q), .in23(X23_q), .in24(X24_q), .in25(X25_q), .in26(X26_q), .in27(X27_q), .in28(X28_q),
    .in29(X29_q), .in30(X30_q), .in31({64{1'b0}}), .out(RegData1), .sel(ReadReg1));
  Multiplexer #(.select(5), .width(64)) multiplexer_2 (
    .in0(reg0), .in1(X1_q), .in2(X2_q), .in3(X3_q), .in4(X4_q), .in5(X5_q), .in6(X6_q), .in7(X7_q),
    .in8(X8_q), .in9(X9_q), .in10(X10_q), .in11(X11_q), .in12(X12_q), .in13(X13_q), .in14(X14_q),
    .in15(X15_q), .in16(X16_q), .in17(X17_q), .in18(X18_q), .in19(X19_q), .in20(X20_q), .in21(X21_q),
    .in22(X22_q), .in23(X23_q), .in24(X24_q), .in25(X25_q), .in26(X26_q), .in27(X27_q), .in28(X28_q),
    .in29(X29_q), .in30(X30_q), .in31({64{1'b0}}), .out(RegData2), .sel(ReadReg2));
  Multiplexer #(.select(5), .width(64)) multiplexer_3 (
    .in0(reg0), .in1(X1_q), .in2(X2_q), .in3(X3_q), .in4(X4_q), .in5(X5_q), .in6(X6_q), .in7(X7_q),
    .in8(X8_q), .in9(X9_q), .in10(X10_q), .in11(X11_q), .in12(X12_q), .in13(X13_q), .in14(X14_q),
    .in15(X15_q), .in16(X16_q), .in17(X17_q), .in18(X18_q), .in19(X19_q), .in20(X20_q), .in21(X21_q),
    .in22(X22_q), .in23(X23_q), .in24(X24_q), .in25(X25_q), .in26(X26_q), .in27(X27_q), .in28(X28_q),
    .in29(X29_q), .in30(X30_q), .in31({64{1'b0}}), .out(RegData3), .sel(ReadReg3));
endmodule

module ADDBrPC (
  input  [10:0] Imm,
  input  [15:0] PC,
  output [15:0] BrPC
);

  wire [15:0] bit_extender_1_out;

  assign bit_extender_1_out = {{5{Imm[10]}}, Imm};  // Bit_Extender bit_extender_1
  Adder #(.width(16)) adder_1 (.a(bit_extender_1_out), .b(PC), .out(BrPC));  // open: cin, cout
endmodule

module ALUMUX (
  input  [63:0] RegData2,
  input  [10:0] Imm,
  input  ALUsrc,
  output [63:0] ALUMUXout
);

  wire [63:0] bit_extender_1_out;

  assign bit_extender_1_out = {{53{Imm[10]}}, Imm};  // Bit_Extender bit_extender_1
  Multiplexer #(.width(64)) multiplexer_1 (.in0(RegData2), .in1(bit_extender_1_out), .out(ALUMUXout), .sel(ALUsrc));
endmodule

module BranchAdder (
  input  in_1
);
endmodule

module BrMUX (
  input  PBr,
  input  Br,
  input  [15:0] NextPC,
  input  [15:0] BrPC,
  input  [63:0] ALUout,
  output [15:0] PCin
);

  wire [15:0] bit_extender_1_out, multiplexer_1_out;

  Multiplexer #(.width(16)) multiplexer_1 (.in0(NextPC), .in1(BrPC), .out(multiplexer_1_out), .sel(Br));
  Bit_Extender #(.in_width(64)) bit_extender_1 (.in(ALUout), .out(bit_extender_1_out));
  Multiplexer #(.width(16)) multiplexer_2 (.in0(multiplexer_1_out), .in1(bit_extender_1_out), .out(PCin), .sel(PBr));
endmodule

module WriteBackMUX (
  input  [63:0] ALUout,
  input  [63:0] ReadDataM,
  input  [15:0] NextPC,
  input  MemToReg,
  input  LinkReg,
  output [63:0] RegDataW
);

  wire [63:0] bit_extender_1_out, multiplexer_1_out;

  Multiplexer #(.width(64)) multiplexer_1 (.in0(ALUout), .in1(ReadDataM), .out(multiplexer_1_out), .sel(MemToReg));
  Multiplexer #(.width(64)) multiplexer_2 (
    .in0(multiplexer_1_out), .in1(bit_extender_1_out), .out(RegDataW), .sel(LinkReg));
  assign bit_extender_1_out = {{48{NextPC[15]}}, NextPC};  // Bit_Extender bit_extender_1
endmodule

module conditionalBranch (
  input  Cbr,
  input  Ubr,
  input  [3:0] conditionCodes,
  input  setCCodes,
  input  Clock,
  output Br
);

  wire C, N, V, Z;

  Register #(.width(4)) register_1 (.D(conditionCodes), .en(setCCodes), .clk(Clock), .Q({N, Z, C, V}));  // open: clr
  buf or_1 (Br, Ubr);  // OR_Gate
endmodule

module DataMemory (
  input  [1:0] bytesToUse,
  input  [63:0] Address,
  input  MemWrite,
  input  Clock,
  input  [63:0] WriteDataM,
  output [63:0] ReadDataM
);

  wire decoder_1_out1, decoder_1_out2, decoder_1_out3, or_1_out, or_2_out;
  wire [7:0] ram_1_p20, ram_1_p21, ram_1_p22, ram_1_p23, ram_1_p24, ram_1_p25, ram_1_p26, ram_1_p27;
  wire [15:0] bit_extender_1_out;
  wire [63:0] bit_extender_2_out, bit_extender_3_out, bit_extender_4_out;

  Decoder #(.enable("false"), .select(2)) decoder_1 (
    .out1(decoder_1_out1), .out2(decoder_1_out2), .out3(decoder_1_out3), .sel(bytesToUse));  // open: out0
  or or_1 (or_1_out, decoder_1_out1, decoder_1_out2, decoder_1_out3);
  or or_2 (or_2_out, decoder_1_out2, decoder_1_out3);
  Bit_Extender #(.in_width(64), .\type ("zero")) bit_extender_1 (.in(Address), .out(bit_extender_1_out));
  // RAM #(.addrWidth(16), .enables("line"), .line("octo"), .misaligned("true")) ram_1: pin names not known; wires that end beside it: bit_extender_1_out, MemWrite, 1'b1, or_1_out, or_2_out, or_2_out, decoder_1_out3, decoder_1_out3, decoder_1_out3, decoder_1_out3, Clock, WriteDataM[7:0], WriteDataM[15:8], WriteDataM[23:16], WriteDataM[31:24], WriteDataM[39:32], WriteDataM[47:40], WriteDataM[55:48], WriteDataM[63:56], ram_1_p20, ram_1_p21, ram_1_p22, ram_1_p23, ram_1_p24, ram_1_p25, ram_1_p26, ram_1_p27
  assign bit_extender_2_out = {{56{1'b0}}, ram_1_p20};  // Bit_Extender bit_extender_2
  assign bit_extender_3_out = {{48{1'b0}}, {ram_1_p21, ram_1_p20}};  // Bit_Extender bit_extender_3
  assign bit_extender_4_out = {{32{1'b0}}, {ram_1_p23, ram_1_p22, ram_1_p21, ram_1_p20}};  // Bit_Extender bit_extender_4
  Multiplexer #(.select(2), .width(64)) multiplexer_1 (
    .in0(bit_extender_2_out), .in1(bit_extender_3_out), .in2(bit_extender_4_out),
    .in3({ram_1_p27, ram_1_p26, ram_1_p25, ram_1_p24, ram_1_p23, ram_1_p22, ram_1_p21, ram_1_p20}),
    .out(ReadDataM), .sel(bytesToUse));

  // Notes on the sheet:
  //   bytesToUse: 00 for 1 byte, 01 for 2 bytes, 10 for 4 bytes, 11 for 8 bytes
endmodule

module ALU2 (
  input  [63:0] B,
  input  [63:0] A,
  input  [1:0] action,
  output [63:0] ALUout,
  output Zflag,
  output [3:0] cCodes,
  output setcodes
);

  wire adder_1_cout, adder_2_cout, bitselector_1_out, bitselector_2_out, bitselector_3_out;
  wire [63:0] B_t, diff, negator_1_out, prod, sum;

  BitSelector #(.width(64)) bitselector_1 (.in(A), .out(bitselector_1_out), .sel({6{1'b1}}));
  Negator #(.width(64)) negator_1 (.in(B), .out(negator_1_out));
  BitSelector #(.width(64)) bitselector_2 (.in(B_t), .out(bitselector_2_out), .sel({6{1'b1}}));
  Multiplexer #(.select(2), .width(64)) multiplexer_1 (
    .in0(B), .in1(B), .in2(B), .in3(negator_1_out), .out(B_t), .sel(action));
  BitSelector #(.width(64)) bitselector_3 (.in(ALUout), .out(bitselector_3_out), .sel({6{1'b1}}));
  Adder #(.width(64)) adder_1 (.a(A), .b(B_t), .out(sum), .cout(adder_1_cout));  // open: cin
  Multiplier #(.width(64)) multiplier_1 (.a(A), .b(B_t), .out(prod));  // open: cin, cout
  Adder #(.width(64)) adder_2 (.a(A), .b(B_t), .out(diff), .cout(adder_2_cout));  // open: cin
  Multiplexer #(.select(2)) multiplexer_2 (
    .in1(adder_1_cout), .in3(adder_2_cout), .out(cCodes[1]), .sel(action));  // open: in0, in2
  VflagCalc vflagcalc_1 (
    .msbA(bitselector_1_out), .msbB(bitselector_2_out), .msbALUout(bitselector_3_out), .Vflag(cCodes[0]));
  Comparator #(.width(64)) comparator_1 (.a(ALUout), .b({64{1'b0}}), .eq(cCodes[2]));  // open: gt, lt
  BitSelector #(.width(64)) bitselector_4 (.in(ALUout), .out(cCodes[3]), .sel({6{1'b1}}));
  Multiplexer #(.select(2), .width(64)) multiplexer_3 (
    .in0(B_t), .in1(sum), .in2(prod), .in3(diff), .out(ALUout), .sel(action));

  assign Zflag = cCodes[2];

  // Other names for the same wires on the sheet: Vflag = cCodes[0]; Cflag = cCodes[1]; Nflag = cCodes[3]

  // Notes on the sheet:
  //   set B to -B if subtraction
  //   to find V:  if the msbs of A and B match BUT not the same as MSB of aluout, then it's 1. IF msb of A and B don't match, then it's always 1
  //   compute outputs and C flag
  //   computer V flag
  //   choose output
  //   Calculate Z flag
  //   calculate N flag
endmodule

module VflagCalc (
  input  msbA,
  input  msbB,
  input  msbALUout,
  output Vflag
);

  wire xnor_1_out, xor_1_out;

  xnor xnor_1 (xnor_1_out, msbA, msbB);
  and and_1 (Vflag, xnor_1_out, xor_1_out);
  xor xor_1 (xor_1_out, msbB, msbALUout);

  // Notes on the sheet:
  //   to find V:  if the msbs of A and B match BUT not the same as MSB of aluout, then it's 1
endmodule

module BLU (
  input  [3:0] Ccodes,
  input  [3:0] action,
  input  ZnotCode,
  output BLUout
);

  wire B_GE, B_GT, B_HI, B_LE, B_LO, B_LS, B_LT, B_NE, CBNZ, not_1_out, not_2_out, not_3_out, not_4_out,
       not_9_out, not_10_out, xor_1_out, xor_2_out, xor_4_out;

  Multiplexer #(.select(4)) multiplexer_1 (
    .in0(Ccodes[2]), .in1(B_NE), .in2(B_LT), .in3(B_LO), .in4(B_LE), .in5(B_LS), .in6(B_GT), .in7(B_HI),
    .in8(B_GE), .in9(Ccodes[1]), .in10(ZnotCode), .in11(CBNZ), .out(BLUout), .sel(action));  // open: in12, in13, in14, in15
  not not_1 (not_1_out, Ccodes[2]);
  xor xor_1 (xor_1_out, Ccodes[0], Ccodes[3]);
  not not_2 (not_2_out, xor_1_out);
  not not_3 (not_3_out, Ccodes[2]);
  xor xor_2 (xor_2_out, Ccodes[0], Ccodes[3]);
  not not_4 (not_4_out, xor_2_out);
  not not_5 (B_NE, Ccodes[2]);
  xor xor_3 (B_LT, Ccodes[0], Ccodes[3]);
  nand nand_1 (B_LE, not_1_out, not_2_out);
  and and_1 (B_GT, not_3_out, not_4_out);
  xor xor_4 (xor_4_out, Ccodes[0], Ccodes[3]);
  not not_6 (B_GE, xor_4_out);
  not not_7 (CBNZ, ZnotCode);
  not not_8 (B_LO, Ccodes[1]);
  not not_9 (not_9_out, Ccodes[2]);
  nand nand_2 (B_LS, not_9_out, Ccodes[1]);
  not not_10 (not_10_out, Ccodes[2]);
  and and_2 (B_HI, not_10_out, Ccodes[1]);

  // Other names for the same wires on the sheet: CBZ = ZnotCode; V = Ccodes[0]; B_HS = Ccodes[1]; C = Ccodes[1];
  //   B_EQ = Ccodes[2]; Z = Ccodes[2]; N = Ccodes[3]

  // Notes on the sheet:
  //   =
  //   !=
  //   <
  //   <=
  //   >
  //   >=
endmodule

module Control (
  input  [10:0] Opcode,
  output Reg2Loc,
  output ALUsrc,
  output [1:0] ALUop,
  output [1:0] bytesToUse,
  output MemWrite,
  output MemToReg,
  output RegWrite,
  output Cbr,
  output Ubr,
  output Pbr,
  output LinkReg,
  output setCodes,
  output [3:0] BLUop
);

  and and_1 (Pbr, Opcode[8], Opcode[7]);

  assign ALUop = Opcode[3:2];
  assign ALUsrc = Opcode[1];
  assign bytesToUse = Opcode[3:2];
  assign Cbr = Opcode[7];
  assign LinkReg = Opcode[9];
  assign MemToReg = Opcode[5];
  assign MemWrite = Opcode[4];
  assign Reg2Loc = Opcode[0];
  assign RegWrite = Opcode[6];
  assign setCodes = Opcode[10];
  assign Ubr = Opcode[8];
endmodule

module Control2 (
  input  [10:0] Opcode,
  output [3:0] BLUop,
  output RegWrite,
  output LinkReg,
  output Pbr,
  output Ubr,
  output Cbr,
  output MemToReg,
  output MemWrite,
  output ALUsrc,
  output Reg2Loc,
  output [3:0] ALUop,
  output [1:0] bytesToUse
);

  wire [1:0] controlbr_1_bytestouse, controlm_1_bytestouse;
  wire [3:0] controlbr_1_aluop, controlbr_1_bluop, controlm_1_aluop, controlm_1_bluop;
  wire [12:4] controlbr_1_regwrite, controlm_1_regwrite;
  wire [18:0] controla_1_bluop, multiplexer_1_out;

  ControlBr controlbr_1 (
    .BCDE(Opcode[3:0]), .BLUop(controlbr_1_bluop), .LinkReg(controlbr_1_regwrite[5]),
    .RegWrite(controlbr_1_regwrite[4]), .Pbr(controlbr_1_regwrite[6]), .ALUop(controlbr_1_aluop),
    .bytesToUse(controlbr_1_bytestouse), .Ubr(controlbr_1_regwrite[7]), .Cbr(controlbr_1_regwrite[8]),
    .MemToReg(controlbr_1_regwrite[9]), .MemWrite(controlbr_1_regwrite[10]),
    .ALUsrc(controlbr_1_regwrite[11]), .Reg2Loc(controlbr_1_regwrite[12]));
  ControlM controlm_1 (
    .BCDE(Opcode[3:0]), .bytesToUse(controlm_1_bytestouse), .ALUop(controlm_1_aluop),
    .BLUop(controlm_1_bluop), .LinkReg(controlm_1_regwrite[5]), .Pbr(controlm_1_regwrite[6]),
    .Ubr(controlm_1_regwrite[7]), .Cbr(controlm_1_regwrite[8]), .Reg2Loc(controlm_1_regwrite[12]),
    .MemWrite(controlm_1_regwrite[10]), .ALUsrc(controlm_1_regwrite[11]), .MemToReg(controlm_1_regwrite[9]),
    .RegWrite(controlm_1_regwrite[4]));
  Multiplexer #(.width(19)) multiplexer_1 (
    .in0({controlm_1_bytestouse, controlm_1_aluop, controlm_1_regwrite, controlm_1_bluop}),
    .in1(controla_1_bluop), .out(multiplexer_1_out), .sel(Opcode[8]));
  Multiplexer #(.width(19)) multiplexer_2 (
    .in0({controlbr_1_bytestouse, controlbr_1_aluop, controlbr_1_regwrite, controlbr_1_bluop}),
    .in1(multiplexer_1_out),
    .out({bytesToUse, ALUop, Reg2Loc, ALUsrc, MemWrite, MemToReg, Cbr, Ubr, Pbr, LinkReg, RegWrite, BLUop}),
    .sel(Opcode[7]));
  ControlA controla_1 (
    .F(Opcode[4]), .G(Opcode[5]), .BCDE(Opcode[3:0]), .ALUop(controla_1_bluop[16:13]),
    .ALUsrc(controla_1_bluop[11]), .Reg2Loc(controla_1_bluop[12]), .BLUop(controla_1_bluop[3:0]),
    .LinkReg(controla_1_bluop[5]), .Pbr(controla_1_bluop[6]), .Ubr(controla_1_bluop[7]),
    .Cbr(controla_1_bluop[8]), .MemWrite(controla_1_bluop[10]), .MemToReg(controla_1_bluop[9]),
    .RegWrite(controla_1_bluop[4]), .bytesToUse(controla_1_bluop[18:17]));

  // Other names for the same wires on the sheet: A = Opcode[0]; B = Opcode[1]; C = Opcode[2]; D = Opcode[3];
  //   E = Opcode[4]; F = Opcode[5]; G = Opcode[6]; H = Opcode[7]; I = Opcode[8]; J = Opcode[9]; K = Opcode[10]

  // Notes on the sheet:
  //   KJ is the classification
  //   0 or 1 for mem or arith
  //   0 for branching
endmodule

module ControlBr (
  input  [3:0] BCDE,
  output [3:0] BLUop,
  output RegWrite,
  output LinkReg,
  output Pbr,
  output Ubr,
  output Cbr,
  output MemToReg,
  output MemWrite,
  output ALUsrc,
  output Reg2Loc,
  output [3:0] ALUop,
  output [1:0] bytesToUse
);

  wire decoder_1_out12, decoder_1_out15;

  Decoder #(.select(4)) decoder_1 (
    .out12(decoder_1_out12), .out13(LinkReg), .out14(Pbr), .out15(decoder_1_out15), .sel(BCDE));  // open: out0, out1, out2, out3, out4, out5, out6, out7, out8, out9, out10, out11, en
  or or_1 (Ubr, decoder_1_out12, LinkReg, Pbr, decoder_1_out15);
  not not_1 (Cbr, Ubr);

  assign ALUop = 4'b0000;
  assign ALUsrc = 1'b0;
  assign BLUop = BCDE;
  assign bytesToUse = 2'b11;
  assign MemToReg = 1'b0;
  assign MemWrite = 1'b0;
  assign Reg2Loc = 1'b0;
  assign RegWrite = LinkReg;

  // Notes on the sheet:
  //   B
  //   BL
  //   unconditional
  //   RET
  //   2 bits
  //   Pbr is for RET
endmodule

module ControlM (
  input  [3:0] BCDE,
  output [1:0] bytesToUse,
  output MemWrite,
  output MemToReg,
  output RegWrite,
  output ALUsrc,
  output LinkReg,
  output Pbr,
  output Ubr,
  output Cbr,
  output Reg2Loc,
  output [3:0] ALUop,
  output [3:0] BLUop
);

  not not_1 (MemToReg, BCDE[2]);

  assign ALUop = 4'b0100;
  assign ALUsrc = BCDE[3];
  assign BLUop = 4'b0100;
  assign bytesToUse = BCDE[1:0];
  assign Cbr = 1'b0;
  assign LinkReg = 1'b0;
  assign MemWrite = BCDE[2];
  assign Pbr = 1'b0;
  assign Reg2Loc = 1'b1;
  assign RegWrite = MemToReg;
  assign Ubr = 1'b0;

  // Notes on the sheet:
  //   2 bits
  //   Pbr is for RET
endmodule

module ControlA (
  input  [3:0] BCDE,
  input  F,
  input  G,
  output [3:0] ALUop,
  output ALUsrc,
  output Reg2Loc,
  output LinkReg,
  output Pbr,
  output Ubr,
  output Cbr,
  output MemWrite,
  output MemToReg,
  output RegWrite,
  output [3:0] BLUop,
  output [1:0] bytesToUse
);

  not not_1 (Reg2Loc, F);

  assign ALUop = BCDE;
  assign ALUsrc = F;
  assign BLUop = 4'b0001;
  assign bytesToUse = 2'b11;
  assign Cbr = 1'b0;
  assign LinkReg = 1'b0;
  assign MemToReg = 1'b0;
  assign MemWrite = 1'b0;
  assign Pbr = 1'b0;
  assign RegWrite = 1'b1;
  assign Ubr = 1'b0;

  // Notes on the sheet:
  //   2 bits
  //   Pbr is for RET
endmodule

module test (
  input  [3:0] in_1,
  input  [3:0] in_2,
  input  [3:0] in_3,
  input  [7:0] in_4,
  output [3:0] out_5
);

  wire binary_to_bcd_converter_1_p2, binary_to_bcd_converter_1_p4, clock_1_out, decoder7seg_1_a,
       decoder7seg_1_b, decoder7seg_1_c, decoder7seg_1_d, decoder7seg_1_dp, decoder7seg_1_e, decoder7seg_1_f,
       decoder7seg_1_g, decoder7seg_2_a, decoder7seg_2_b, decoder7seg_2_c, decoder7seg_2_d, decoder7seg_2_dp,
       decoder7seg_2_e, decoder7seg_2_f, decoder7seg_2_g, decoder7seg_3_a, decoder7seg_3_b, decoder7seg_3_c,
       decoder7seg_3_d, decoder7seg_3_dp, decoder7seg_3_e, decoder7seg_3_f, decoder7seg_3_g, decoder7seg_4_a,
       decoder7seg_4_b, decoder7seg_4_c, decoder7seg_4_d, decoder7seg_4_dp, decoder7seg_4_e, decoder7seg_4_f,
       decoder7seg_4_g, decoder7seg_5_a, decoder7seg_5_b, decoder7seg_5_c, decoder7seg_5_d, decoder7seg_5_dp,
       decoder7seg_5_e, decoder7seg_5_f, decoder7seg_5_g, decoder7seg_6_a, decoder7seg_6_b, decoder7seg_6_c,
       decoder7seg_6_d, decoder7seg_6_dp, decoder7seg_6_e, decoder7seg_6_f, decoder7seg_6_g, decoder7seg_7_a,
       decoder7seg_7_b, decoder7seg_7_c, decoder7seg_7_d, decoder7seg_7_dp, decoder7seg_7_e, decoder7seg_7_f,
       decoder7seg_7_g, decoder7seg_8_a, decoder7seg_8_b, decoder7seg_8_c, decoder7seg_8_d, decoder7seg_8_dp,
       decoder7seg_8_e, decoder7seg_8_f, decoder7seg_8_g, keyboard_1_avail, rgbled_1_p1;
  wire [6:0] keyboard_1_data;
  wire [7:0] charto7seg_2_num, charto7seg_3_num, charto7seg_4_num, charto7seg_5_num, charto7seg_6_num,
       charto7seg_7_num, charto7seg_8_num, charto7seg_9_num, undriven, undriven_2, undriven_3, undriven_4,
       undriven_5, undriven_6, undriven_7, undriven_8;

  charTo7Seg charto7seg_1 ();  // open: char, num
  _7_Segment_Display u_7_segment_display_1 (
    .g(decoder7seg_1_g), .f(decoder7seg_1_f), .a(decoder7seg_1_a), .b(decoder7seg_1_b), .e(decoder7seg_1_e),
    .d(decoder7seg_1_d), .c(decoder7seg_1_c), .dp(decoder7seg_1_dp));
  decoder7Seg decoder7seg_1 (
    .num(charto7seg_2_num), .F(decoder7seg_1_f), .G(decoder7seg_1_g), .E(decoder7seg_1_e),
    .D(decoder7seg_1_d), .A(decoder7seg_1_a), .B(decoder7seg_1_b), .DP(decoder7seg_1_dp), .C(decoder7seg_1_c));
  _7_Segment_Display u_7_segment_display_2 (
    .g(decoder7seg_2_g), .f(decoder7seg_2_f), .a(decoder7seg_2_a), .b(decoder7seg_2_b), .e(decoder7seg_2_e),
    .d(decoder7seg_2_d), .c(decoder7seg_2_c), .dp(decoder7seg_2_dp));
  charTo7Seg charto7seg_2 (.char(undriven_8), .num(charto7seg_2_num));
  decoder7Seg decoder7seg_2 (
    .num(charto7seg_3_num), .F(decoder7seg_2_f), .G(decoder7seg_2_g), .E(decoder7seg_2_e),
    .D(decoder7seg_2_d), .A(decoder7seg_2_a), .B(decoder7seg_2_b), .DP(decoder7seg_2_dp), .C(decoder7seg_2_c));
  decoder7Seg decoder7seg_3 (
    .num(charto7seg_4_num), .F(decoder7seg_3_f), .G(decoder7seg_3_g), .E(decoder7seg_3_e),
    .D(decoder7seg_3_d), .A(decoder7seg_3_a), .B(decoder7seg_3_b), .DP(decoder7seg_3_dp), .C(decoder7seg_3_c));
  _7_Segment_Display u_7_segment_display_3 (
    .g(decoder7seg_3_g), .f(decoder7seg_3_f), .a(decoder7seg_3_a), .b(decoder7seg_3_b), .e(decoder7seg_3_e),
    .d(decoder7seg_3_d), .c(decoder7seg_3_c), .dp(decoder7seg_3_dp));
  _7_Segment_Display u_7_segment_display_4 (
    .g(decoder7seg_4_g), .f(decoder7seg_4_f), .a(decoder7seg_4_a), .b(decoder7seg_4_b), .e(decoder7seg_4_e),
    .d(decoder7seg_4_d), .c(decoder7seg_4_c), .dp(decoder7seg_4_dp));
  charTo7Seg charto7seg_3 (.char(undriven_7), .num(charto7seg_3_num));
  charTo7Seg charto7seg_4 (.char(undriven_6), .num(charto7seg_4_num));
  decoder7Seg decoder7seg_4 (
    .num(charto7seg_5_num), .F(decoder7seg_4_f), .G(decoder7seg_4_g), .E(decoder7seg_4_e),
    .D(decoder7seg_4_d), .A(decoder7seg_4_a), .B(decoder7seg_4_b), .DP(decoder7seg_4_dp), .C(decoder7seg_4_c));
  decoder7Seg decoder7seg_5 (
    .num(charto7seg_6_num), .F(decoder7seg_5_f), .G(decoder7seg_5_g), .E(decoder7seg_5_e),
    .D(decoder7seg_5_d), .A(decoder7seg_5_a), .B(decoder7seg_5_b), .DP(decoder7seg_5_dp), .C(decoder7seg_5_c));
  _7_Segment_Display u_7_segment_display_5 (
    .g(decoder7seg_5_g), .f(decoder7seg_5_f), .a(decoder7seg_5_a), .b(decoder7seg_5_b), .e(decoder7seg_5_e),
    .d(decoder7seg_5_d), .c(decoder7seg_5_c), .dp(decoder7seg_5_dp));
  charTo7Seg charto7seg_5 (.char(undriven_5), .num(charto7seg_5_num));
  charTo7Seg charto7seg_6 (.char(undriven_4), .num(charto7seg_6_num));
  assign out_5 = in_1 ^ in_2;  // XOR_Gate xor_1, 4 bits wide
  // NoConnect on nothing
  decoder7Seg decoder7seg_6 (
    .num(charto7seg_7_num), .F(decoder7seg_6_f), .G(decoder7seg_6_g), .E(decoder7seg_6_e),
    .D(decoder7seg_6_d), .A(decoder7seg_6_a), .B(decoder7seg_6_b), .DP(decoder7seg_6_dp), .C(decoder7seg_6_c));
  _7_Segment_Display u_7_segment_display_6 (
    .g(decoder7seg_6_g), .f(decoder7seg_6_f), .a(decoder7seg_6_a), .b(decoder7seg_6_b), .e(decoder7seg_6_e),
    .d(decoder7seg_6_d), .c(decoder7seg_6_c), .dp(decoder7seg_6_dp));
  _7_Segment_Display u_7_segment_display_7 (
    .g(decoder7seg_7_g), .f(decoder7seg_7_f), .a(decoder7seg_7_a), .b(decoder7seg_7_b), .e(decoder7seg_7_e),
    .d(decoder7seg_7_d), .c(decoder7seg_7_c), .dp(decoder7seg_7_dp));
  charTo7Seg charto7seg_7 (.char(undriven_3), .num(charto7seg_7_num));
  _7_Segment_Display u_7_segment_display_8 ();  // open: g, f, a, b, e, d, c, dp
  // BCD_to_7_Segment_decoder bcd_to_7_segment_decoder_1: pin names not known; wires that end beside it: in_3
  decoder7Seg decoder7seg_7 (
    .num(charto7seg_8_num), .F(decoder7seg_7_f), .G(decoder7seg_7_g), .E(decoder7seg_7_e),
    .D(decoder7seg_7_d), .A(decoder7seg_7_a), .B(decoder7seg_7_b), .DP(decoder7seg_7_dp), .C(decoder7seg_7_c));
  decoder7Seg decoder7seg_8 (
    .num(charto7seg_9_num), .F(decoder7seg_8_f), .G(decoder7seg_8_g), .E(decoder7seg_8_e),
    .D(decoder7seg_8_d), .A(decoder7seg_8_a), .B(decoder7seg_8_b), .DP(decoder7seg_8_dp), .C(decoder7seg_8_c));
  _7_Segment_Display u_7_segment_display_9 (
    .g(decoder7seg_8_g), .f(decoder7seg_8_f), .a(decoder7seg_8_a), .b(decoder7seg_8_b), .e(decoder7seg_8_e),
    .d(decoder7seg_8_d), .c(decoder7seg_8_c), .dp(decoder7seg_8_dp));
  charTo7Seg charto7seg_8 (.char(undriven_2), .num(charto7seg_8_num));
  charTo7Seg charto7seg_9 (.char(undriven), .num(charto7seg_9_num));
  // Binary_to_BCD_converter #(.binvalue(8)) binary_to_bcd_converter_1: pin names not known; wires that end beside it: in_4, binary_to_bcd_converter_1_p2, binary_to_bcd_converter_1_p2, binary_to_bcd_converter_1_p4, binary_to_bcd_converter_1_p4
  Hex_Digit_Display hex_digit_display_1 ();  // open: value, dp
  Joystick joystick_1 ();  // open: x, y
  // RGB_Video rgb_video_1: pin names not known
  // BCD_to_7_Segment_decoder bcd_to_7_segment_decoder_2: pin names not known
  // RGBLED rgbled_1: pin names not known; wires that end beside it: rgbled_1_p1, rgbled_1_p1
  _7_Segment_Display u_7_segment_display_10 ();  // open: g, f, a, b, e, d, c, dp
  // PortIO portio_1: pin names not known; wires that end beside it: 1'b1
  Clock clock_1 (.out(clock_1_out));
  Keyboard keyboard_1 (.clk(clock_1_out), .avail(keyboard_1_avail), .data(keyboard_1_data));  // open: re, clr
  DipSwitch dipswitch_1 ();  // open: sw1, sw2, sw3, sw4, sw5, sw6, sw7, sw8
  // Digital_Oscilloscope digital_oscilloscope_1: pin names not known
  // PlaRom plarom_1: pin names not known; wires that end beside it: keyboard_1_avail, keyboard_1_data
endmodule

module ALU3 (
  input  clock,
  input  [63:0] A,
  input  [63:0] B,
  input  [3:0] action,
  output [3:0] cCodes,
  output [63:0] ALUout,
  output Zflag
);

  wire bitselector_1_out, bitselector_2_out, bitselector_3_out, cADD, comparator_1_eq, comparator_2_eq, cSUB,
       multiplexer_1_out, not_1_out, setcodes;
  wire [3:0] cCodes_t;
  wire [5:0] bit_extender_1_out;
  wire [63:0] ADD, ANDD, ASR, EOR, LSL, LSR, MUL, not_2_out, ORR, SDIV, SUB, UDIV, undriven;

  BitSelector #(.width(64)) bitselector_1 (.in(A), .out(bitselector_1_out), .sel({6{1'b1}}));
  Register #(.width(4)) register_1 (
    .D({cCodes_t[3], Zflag, cCodes_t[1:0]}), .en(setcodes), .clk(clock), .Q(cCodes));  // open: clr
  BitSelector #(.width(64)) bitselector_2 (.in(B), .out(bitselector_2_out), .sel({6{1'b1}}));
  not not_1 (not_1_out, bitselector_2_out);
  Comparator #(.width(4)) comparator_1 (.a(action), .b(4'b1110), .eq(comparator_1_eq));  // open: gt, lt
  Multiplexer multiplexer_1 (.in0(bitselector_2_out), .in1(not_1_out), .out(multiplexer_1_out), .sel(comparator_1_eq));
  and and_1 (setcodes, action[2], action[3]);
  BitSelector #(.width(64)) bitselector_3 (.in(ALUout), .out(bitselector_3_out), .sel({6{1'b1}}));
  Bit_Extender #(.in_width(64), .out_width(6)) bit_extender_1 (.in(B), .out(bit_extender_1_out));
  Comparator #(.width(4)) comparator_2 (.a(action), .b(4'b1110), .eq(comparator_2_eq));  // open: gt, lt
  assign not_2_out = ~B;  // NOT_Gate not_2, 64 bits wide
  VflagCalc vflagcalc_1 (
    .msbA(bitselector_1_out), .msbB(multiplexer_1_out), .msbALUout(bitselector_3_out), .Vflag(cCodes_t[0]));
  Multiplexer multiplexer_2 (.in0(cADD), .in1(cSUB), .out(cCodes_t[1]), .sel(comparator_2_eq));
  assign ORR = A | B;  // OR_Gate or_1, 64 bits wide
  assign EOR = A ^ B;  // XOR_Gate xor_1, 64 bits wide
  assign ANDD = A & B;  // AND_Gate and_2, 64 bits wide
  Adder #(.width(64)) adder_1 (.a(A), .b(B), .out(ADD), .cout(cADD));  // open: cin
  Adder #(.width(64)) adder_2 (.a(A), .b(not_2_out), .out(SUB), .cin(1'b1), .cout(cSUB));
  Multiplier #(.width(64)) multiplier_1 (.a(A), .b(B), .out(MUL));  // open: cin, cout
  Divider #(.mode("twosComplement"), .width(64)) divider_1 (.a(A), .b(B), .out(SDIV));  // open: upper, rem
  Divider #(.width(64)) divider_2 (.a(A), .b(B), .out(UDIV));  // open: upper, rem
  Shifter #(.width(64)) shifter_1 (.in(A), .\dist (bit_extender_1_out), .out(LSL));
  Shifter #(.shift("lr"), .width(64)) shifter_2 (.in(A), .\dist (bit_extender_1_out), .out(LSR));
  Shifter #(.shift("ar"), .width(64)) shifter_3 (.in(A), .\dist (bit_extender_1_out), .out(ASR));
  Multiplexer #(.select(4), .width(64)) multiplexer_3 (
    .in0(B), .in1(ORR), .in2(EOR), .in3(ANDD), .in4(ADD), .in5(SUB), .in6(MUL), .in7(SDIV), .in8(UDIV),
    .in9(LSL), .in10(LSR), .in11(ASR), .in12(ANDD), .in13(ADD), .in14(SUB), .in15(undriven), .out(ALUout),
    .sel(action));
  Comparator #(.width(64)) comparator_3 (.a(ALUout), .b({64{1'b0}}), .eq(Zflag));  // open: gt, lt
  BitSelector #(.width(64)) bitselector_4 (.in(ALUout), .out(cCodes_t[3]), .sel({6{1'b1}}));

  // Other names for the same wires on the sheet: Vflag = cCodes_t[0]; Cflag = cCodes_t[1]; cCodes_t[2] = Zflag;
  //   Nflag = cCodes_t[3]; passB[63:0] = B

  // Notes on the sheet:
  //   MOV (passB)
  //   ORR
  //   EOR
  //   AND
  //   ADD
  //   SUB
  //   MUL
  //   SDIV
  //   UDIV
  //   LSL
  //   LSR
  //   ASR
  //   ANDS
  //   ADDS
  //   SUBS
  //   calculate V flag
  //   0000
  //   0100
  //   1000
  //   1100
  //   1101
  //   1110
  //   1111
  //   calculate c flag
  //   Calculate Z flag
  //   calculate N flag
endmodule

module charTo7Seg (
  input  [7:0] char,
  output [7:0] num
);

  wire decoder7seg_1_a, decoder7seg_1_b, decoder7seg_1_c, decoder7seg_1_d, decoder7seg_1_dp, decoder7seg_1_e,
       decoder7seg_1_f, decoder7seg_1_g;
  wire [7:0] multiplexer_2_out, multiplexer_3_p4, multiplexer_4_out, multiplexer_5_out;

  _7_Segment_Display u_7_segment_display_1 (
    .g(decoder7seg_1_g), .f(decoder7seg_1_f), .a(decoder7seg_1_a), .b(decoder7seg_1_b), .e(decoder7seg_1_e),
    .d(decoder7seg_1_d), .c(decoder7seg_1_c), .dp(decoder7seg_1_dp));
  decoder7Seg decoder7seg_1 (
    .num(num), .F(decoder7seg_1_f), .G(decoder7seg_1_g), .E(decoder7seg_1_e), .D(decoder7seg_1_d),
    .A(decoder7seg_1_a), .B(decoder7seg_1_b), .DP(decoder7seg_1_dp), .C(decoder7seg_1_c));
  Multiplexer #(.select(2), .width(8)) multiplexer_1 (
    .in0(multiplexer_2_out), .in1(multiplexer_4_out), .in2(multiplexer_5_out), .in3(multiplexer_3_p4),
    .out(num), .sel(char[6:5]));
  Multiplexer #(.select(5), .width(8)) multiplexer_2 (
    .out(multiplexer_2_out), .sel(char[4:0]));  // open: in0, in1, in2, in3, in4, in5, in6, in7, in8, in9, in10, in11, in12, in13, in14, in15, in16, in17, in18, in19, in20, in21, in22, in23, in24, in25, in26, in27, in28, in29, in30, in31
  // Multiplexer #(.select(5), .width(8)) multiplexer_3: pin names not known; wires that end beside it: {8{1'b1}}, {8{1'b1}}, char[4:0], multiplexer_3_p4, {8{1'b1}}, {8{1'b1}}
  Multiplexer #(.select(5), .width(8)) multiplexer_4 (
    .in0({8{1'b0}}), .in1(8'h86), .in2(8'h22), .in3(8'h7e), .in4(8'h6d), .in5(8'hd2), .in6(8'h46),
    .in7(8'h20), .in8(8'h29), .in9(8'hb), .in10(8'h21), .in11(8'h70), .in12(8'h10), .in13(8'h40),
    .in14(8'h80), .in15(8'h52), .in16(8'h3f), .in17(8'h6), .in18(8'h5b), .in19(8'h4f), .in20(8'h66),
    .in21(8'h6d), .in22(8'h7d), .in23(8'h7), .in24(8'h7f), .in25(8'h6f), .in26(8'h9), .in27(8'hd),
    .in28(8'h61), .in29(8'h48), .in30(8'h43), .in31(8'hd3), .out(multiplexer_4_out), .sel(char[4:0]));
  Multiplexer #(.select(5), .width(8)) multiplexer_5 (
    .in0(8'h5f), .in1(8'h77), .in2(8'h7c), .in3(8'h39), .in4(8'h5e), .in5(8'h79), .in6(8'h71), .in7(8'h3d),
    .in8(8'h76), .in9(8'h30), .in10(8'h1e), .in11(8'h75), .in12(8'h38), .in13(8'h15), .in14(8'h37),
    .in15(8'h3f), .in16(8'h73), .in17(8'h6b), .in18(8'h33), .in19(8'h6d), .in20(8'h78), .in21(8'h3e),
    .in22(8'h3e), .in23(8'h2a), .in24(8'h76), .in25(8'h6e), .in26(8'h5b), .in27(8'h39), .in28(8'h64),
    .in29(8'hf), .in30(8'h23), .in31(8'h8), .out(multiplexer_5_out), .sel(char[4:0]));

  // Other names for the same wires on the sheet: bit56[1:0] = char[6:5]; bits0to4[4:0] = char[4:0]

  // Notes on the sheet:
  //   * U */ 0x3E, /* V */ 0x2A, /* W */ 0x76, /* X */ 0x6E, /* Y */ 0x5B, /* Z */ 0x39, /* [ */ 0x64, /* \ */ 0x0F, /* ] */ 0x23, /* ^ */ 0x08, /* _ */ 0x02, /* ` */ 0x5F, /* a */ 0x7C, /* b */ 0x58, /* c */ 0x5E, /* d */ 0x7B, /* e */ 0x71, /* f */ 0x6F, /* g */ 0x74, /* h */ 0x10, /* i */ 0x0C, /* j */ 0x75, /* k */ 0x30, /* l */ 0x14, /* m */ 0x54, /* n */ 0x5C, /* o */ 0x73, /* p */ 0x67, /* q */ 0x50, /* r */ 0x6D, /* s */ 0x78, /* t */ 0x1C, /* u */ 0x1C, /* v */ 0x14, /* w */ 0x76, /* x */ 0x6E, /* y */ 0x5B, /* z */ 0x46, /* { */ 0x30, /* | */ 0x70, / } */ 0x01, /* ~ */
  //   space
  //   null-unitseparator
  //   '-DEL
  //   space-?
  //   @-_
endmodule

module decoder7Seg (
  input  [7:0] num,
  output F,
  output A,
  output G,
  output B,
  output E,
  output DP,
  output D,
  output C
);

  _7_Segment_Display u_7_segment_display_1 (
    .g(num[6]), .f(num[5]), .a(num[0]), .b(num[1]), .e(num[4]), .d(num[3]), .c(num[2]), .dp(num[7]));

  assign A = num[0];
  assign B = num[1];
  assign C = num[2];
  assign D = num[3];
  assign DP = num[7];
  assign E = num[4];
  assign F = num[5];
  assign G = num[6];
endmodule
